# Fritzing sketch Breadboard layout (saved by Fritzing 0.9.3b)
breadboards: 1

parts:
  BAT1 = Battery Holders [package=lipo-1100mAh]  # not connected
  DS1 = DS18B20 1-Wire Temperature Sensor Probe Cable
  S1 = Reed switch [package=THT]
  R2 = Resistor [tolerance=±5% resistance=100 package=THT]
  R3 = Resistor [tolerance=±5% resistance=4.7 package=THT]
  DS2 = DS18B20 1-Wire Temperature Sensor [part_number=DS18B20]
  Part2 = Adafruit Feather 32u4 FONA [part_number="Adafruit #3027"]
  J1 = Basic Force Sensing Resistor (FSR) [package=THT]
  R4 = Resistor [tolerance=±5% resistance=10k package=THT]

nets:
  GND: DS1.GND, R2.Pin_1, DS2.GND, Part2.GND, R4.Pin_1
  VDD: DS1.VDD, S1.pin_1, R3.Pin_1, DS2.DQ, Part2.+3V3, J1.pin_0
  N1: DS1.shield, R3.Pin_0, Part2.2
  N2: S1.pin_2, R2.Pin_0, Part2.A5
  N3: DS2.VDD, Part2.3
  N4: Part2.A4, J1.pin_1, R4.Pin_0

custom parts:
  Adafruit Feather 32u4 FONA: This is the Adafruit Feather 32u4 FONA - our take on an 'all-in-one' Arduino-compatible + audio/sms/data capable cellular with built in USB and battery charging. Its an Adafruit Feather 32u4 with a FONA800 module, ready to rock! We have other boards and accessories in the Feather family, check'em out here. At the Feather 32u4's heart is at ATmega32u4 clocked at 8 MHz and at 3.3V logic, a chip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
