# Fritzing sketch Breadboard - Step 1 (saved by Fritzing 0.9.3b)
circuit board: 8.46667cm x 5.64444cm
breadboards: 1

parts:
  BAT1 = Battery Holders [package=lipo-1100mAh]  # not connected
  R2 = Resistor [tolerance=±5% resistance=100 package=THT]
  R3 = Resistor [tolerance=±5% resistance=4.7 package=THT]
  Part2 = Adafruit Feather 32u4 FONA [part_number="Adafruit #3027"]
  R4 = Resistor [tolerance=±5% resistance=10k package=THT]
  J2 = Camdenboss CTB0158-10 [part_number=CTB0158-10 package=THT]

nets:
  N1: R2.Pin_0, Part2.A5, J2.terminal_8
  N2: R2.Pin_1, Part2.GND, R4.Pin_1, J2.terminal_2, J2.terminal_5
  N3: R3.Pin_0, Part2.2, J2.terminal_4
  N4: R3.Pin_1, Part2.+3V3, J2.terminal_3, J2.terminal_6, J2.terminal_7, J2.terminal_9
  N5: Part2.A4, R4.Pin_0, J2.terminal_10
  N6: Part2.3, J2.terminal_1

custom parts:
  Adafruit Feather 32u4 FONA: This is the Adafruit Feather 32u4 FONA - our take on an 'all-in-one' Arduino-compatible + audio/sms/data capable cellular with built in USB and battery charging. Its an Adafruit Feather 32u4 with a FONA800 module, ready to rock! We have other boards and accessories in the Feather family, check'em out here. At the Feather 32u4's heart is at ATmega32u4 clocked at 8 MHz and at 3.3V logic, a chip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
