# Fritzing sketch Step 2 (saved by Fritzing 0.9.3b)
breadboards: 1

parts:
  R5 = Resistor [tolerance=±5% resistance=100 package=THT]
  R6 = Resistor [tolerance=±5% resistance=10k package=THT]
  J3 = Camdenboss CTB0158-10 [part_number=CTB0158-10 package=THT]
  R7 = Resistor [tolerance=±5% resistance=4.7 package=THT]

nets:
  N1: R5.Pin_0, J3.terminal_8
  N2: R5.Pin_1, R6.Pin_1, J3.terminal_2, J3.terminal_5
  N3: R6.Pin_0, J3.terminal_10
  N4: J3.terminal_3, J3.terminal_6, J3.terminal_7, J3.terminal_9, R7.Pin_1
  N5: J3.terminal_4, R7.Pin_0
