# Fritzing sketch Step 4 (saved by Fritzing 0.9.3b)
breadboards: 1

parts:
  R5 = Resistor [tolerance=±5% resistance=100 package=THT]
  R6 = Resistor [tolerance=±5% resistance=10k package=THT]
  J3 = Camdenboss CTB0158-10 [part_number=CTB0158-10 package=THT]
  R7 = Resistor [tolerance=±5% resistance=4.7 package=THT]
  Part3 = Adafruit Feather 32u4 FONA [part_number="Adafruit #3027"]
  LED2 = LED - 3mm [color="Green (570nm)" package="3 mm [THT]"]
  LED3 = LED - 3mm [color="Red (633nm)" package="3 mm [THT]"]  # not connected
  LED4 = LED - 3mm [color="Red (633nm)" package="3 mm [THT]"]  # not connected
  LED5 = LED - 3mm [color="Red (633nm)" package="3 mm [THT]"]  # not connected
  LED6 = LED - 3mm [color="Blue (525nm)" package="3 mm [THT]"]
  LED7 = LED - 3mm [color="Red (633nm)" package="3 mm [THT]"]

nets:
  N1: R5.Pin_0, J3.terminal_8, Part3.A5
  N2: R5.Pin_1, R6.Pin_1, J3.terminal_2, J3.terminal_5, Part3.GND
  N3: R6.Pin_0, J3.terminal_10, Part3.A4
  N4: J3.terminal_1, Part3.3
  N5: J3.terminal_3, J3.terminal_6, J3.terminal_7, J3.terminal_9, R7.Pin_1, Part3.+3V3
  N6: J3.terminal_4, R7.Pin_0, Part3.2
  N7: Part3.13, LED6.anode
  N8: Part3.12, LED2.anode
  N9: Part3.11, LED7.anode
  N10: LED2.cathode, LED6.cathode, LED7.cathode

custom parts:
  Adafruit Feather 32u4 FONA: This is the Adafruit Feather 32u4 FONA - our take on an 'all-in-one' Arduino-compatible + audio/sms/data capable cellular with built in USB and battery charging. Its an Adafruit Feather 32u4 with a FONA800 module, ready to rock! We have other boards and accessories in the Feather family, check'em out here. At the Feather 32u4's heart is at ATmega32u4 clocked at 8 MHz and at 3.3V logic, a chip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
